# Fritzing sketch ESP32_dev_board_2x19_GPIO_work (saved by Fritzing 0.9.3b)
breadboards: 1

parts:
  IC1 = IC, DIP package, 38 pins [chip_label="ESP32 dev board"]
  RESET = Pushbutton [package="[THT]"]
  R1 = Resistor [tolerance=±5% resistance=22k package=THT]
  R2 = Resistor [tolerance=±2% resistance=10k package=THT]
  R3 = Resistor [tolerance=±5% resistance=220 package=THT]
  R4 = Resistor [tolerance=±5% resistance=220 package=THT]
  R5 = Resistor [tolerance=±5% resistance=22k package=THT]
  R6 = Resistor [tolerance=±5% resistance=22k package=THT]
  R7 = Resistor [tolerance=±5% resistance=22k package=THT]
  R8 = Resistor [tolerance=±5% resistance=22k package=THT]
  R10 = Resistor [tolerance=±5% resistance=47k package=THT]
  trimm = Rotary Potentiometer (Small) [maximum_resistance=10kΩ package=THT]
  C1 = Ceramic Capacitor [capacitance=10nF package="100 mil [THT, multilayer]"]
  R12 = Resistor [tolerance=±5% resistance=22k package=THT]
  R13 = Resistor [tolerance=±5% resistance=22k package=THT]
  R14 = Resistor [tolerance=±5% resistance=22k package=THT]  # not connected
  R15 = Resistor [tolerance=±5% resistance=220 package=THT]  # not connected

nets:
  3.3V: IC1.pin1
  RESET: IC1.pin2, RESET.Pin_1, RESET.Pin_2
  VU_SENS GPIO36: IC1.pin3
  MORSE GPIO39: IC1.pin4
  MAGIC TRIGGER GPIO34: IC1.pin5
  OTHER: IC1.pin6
  DAC1: IC1.pin9
  DAC2: IC1.pin10
  PERIPH_PWR: IC1.pin13
  N1: IC1.pin23, R1.Pin_0
  N2: IC1.pin24, R2.Pin_0
  N3: IC1.pin25, R3.Pin_0
  N4: IC1.pin26, R4.Pin_0
  N5: IC1.pin27, R5.Pin_0
  N6: IC1.pin28, R6.Pin_0
  N7: IC1.pin29, R7.Pin_0
  N8: IC1.pin30, R8.Pin_0
  N9: IC1.pin31, R12.Pin_0
  I2C: IC1.pin33, IC1.pin36
  GND: RESET.Pin_3, RESET.Pin_4, trimm.leg2, C1.0
  N10: R1.Pin_1, R2.Pin_1, R3.Pin_1, R4.Pin_1, R5.Pin_1, R6.Pin_1, R10.Pin_0
  N11: R7.Pin_1, R8.Pin_1, R13.Pin_0
  N12: R10.Pin_1, trimm.leg1, C1.1
  GPIO AUDIO LOWER: trimm.wiper
  N13: R12.Pin_1, R13.Pin_1

notes:
  WiFi
  USB
